# Fritzing sketch cube_circuit (saved by Fritzing 0.9.3b)
perfboards: 1

parts:
  R1 = Resistor [tolerance=±5% resistance=1k package=THT]
  C1 = Ceramic Capacitor [capacitance=100nF voltage=50V package="100 mil [THT, multilayer]"]
  U1 = 74HC595 [package="DIP16 [THT]"]
  U2 = 74HC595 [package="DIP16 [THT]"]
  Arduino = Arduino Uno (Rev3)
  C2 = Ceramic Capacitor [capacitance=100nF voltage=50V package="100 mil [THT, multilayer]"]
  R2 = Resistor [tolerance=±5% resistance=1k package=THT]
  R3 = Resistor [tolerance=±5% resistance=1k package=THT]
  R4 = Resistor [tolerance=±5% resistance=1k package=THT]
  R5 = Resistor [tolerance=±5% resistance=1k package=THT]
  R6 = Resistor [tolerance=±5% resistance=1k package=THT]
  R7 = Resistor [tolerance=±5% resistance=1k package=THT]
  R8 = Resistor [tolerance=±5% resistance=1k package=THT]
  R9 = Resistor [tolerance=±5% resistance=1k package=THT]
  R10 = Resistor [tolerance=±5% resistance=1k package=THT]
  R11 = Resistor [tolerance=±5% resistance=1k package=THT]
  R12 = Resistor [tolerance=±5% resistance=1k package=THT]
  R13 = Resistor [tolerance=±5% resistance=1k package=THT]
  R14 = Resistor [tolerance=±5% resistance=1k package=THT]
  R15 = Resistor [tolerance=±5% resistance=1k package=THT]
  R16 = Resistor [tolerance=±5% resistance=1k package=THT]
  J2 = male pin header, 4 pins [form="♂ (male)"]
  J3 = male pin header, 4 pins [form="♂ (male)"]
  J4 = male pin header, 4 pins [form="♂ (male)"]
  J5 = male pin header, 4 pins [form="♂ (male)"]
  J8 = female pin header, 4 pins [form="♀ (female)"]
  J7 = female pin header, 5 pins [form="♀ (female)"]
  J1 = male pin header, 5 pins [form="♂ (male)"]
  J7_2 = male pin header, 4 pins [form="♂ (male)"]
  J10 = male pin header, 4 pins [form="♂ (male)"]

nets:
  N1: R1.Pin_0, J2.pin1
  N2: R1.Pin_1, U1.Q0
  GND: C1.0, U1.GND, U1.OE, U2.GND, U2.OE, C2.0, J1.pin2
  VCC: C1.1, U1.MR, U1.VCC, U2.MR, U2.VCC, C2.1, J1.pin1
  N3: U1.Q1, R2.Pin_1
  N4: U1.Q2, R3.Pin_1
  N5: U1.Q3, R4.Pin_1
  N6: U1.Q4, R5.Pin_1
  N7: U1.Q5, R6.Pin_1
  N8: U1.Q6, R7.Pin_1
  N9: U1.Q7, R8.Pin_1
  N10: U1.Q7', U2.DS
  N11: U1.SH_CP, U2.SH_CP, J1.pin4
  N12: U1.ST_CP, U2.ST_CP, J1.pin5
  N13: U1.DS, J1.pin3
  N14: U2.Q1, R15.Pin_1
  N15: U2.Q2, R12.Pin_1
  N16: U2.Q3, R11.Pin_1
  N17: U2.Q4, R13.Pin_1
  N18: U2.Q5, R9.Pin_1
  N19: U2.Q6, R16.Pin_1
  N20: U2.Q7, R14.Pin_1
  N21: U2.Q0, R10.Pin_1
  N22: Arduino.D9_PWM, J7.pin3
  N23: Arduino.D11_PWM/MOSI, J7.pin4
  N24: Arduino.D12/MISO, J7.pin5
  N25: Arduino.D2, J8.pin1
  N26: Arduino.D3_PWM, J8.pin2
  N27: Arduino.D4, J8.pin3
  N28: Arduino.D5_PWM, J8.pin4
  N29: Arduino.5V, J7.pin1
  N30: Arduino.GND, J7.pin2
  N31: R2.Pin_0, J2.pin2
  N32: R3.Pin_0, J2.pin3
  N33: R4.Pin_0, J2.pin4
  N34: R5.Pin_0, J3.pin1
  N35: R6.Pin_0, J3.pin2
  N36: R7.Pin_0, J3.pin3
  N37: R8.Pin_0, J3.pin4
  N38: R9.Pin_0, J5.pin2
  N39: R10.Pin_0, J4.pin1
  N40: R11.Pin_0, J4.pin4
  N41: R12.Pin_0, J4.pin3
  N42: R13.Pin_0, J5.pin1
  N43: R14.Pin_0, J5.pin4
  N44: R15.Pin_0, J4.pin2
  N45: R16.Pin_0, J5.pin3
  N46: J7_2.pin1, J10.pin1
  N47: J7_2.pin2, J10.pin2
  N48: J7_2.pin3, J10.pin3
  N49: J7_2.pin4, J10.pin4

notes:
  LED Cathode
  Arduino Digital
  Arduino Main
  Main
  LED Common
